// Logisim project MIPS-logisim.circ as structural Verilog: 10 circuits, main circuit main
module adder32 (
  input  in_Cin,
  input  [31:0] in_A,
  input  [31:0] in_B,
  output [31:0] out_F,
  output out_SF,
  output out_CF,
  output out_ZF,
  output out_OF
);

  wire adder_1_cout, adder_2_cout, adder_3_cout, adder_4_cout;

  Adder adder_1 (.a(in_A[7:0]), .b(in_B[7:0]), .out(out_F[7:0]), .cin(in_Cin), .cout(adder_1_cout));
  Adder adder_2 (.a(in_A[15:8]), .b(in_B[15:8]), .out(out_F[15:8]), .cin(adder_1_cout), .cout(adder_2_cout));
  Adder adder_3 (.a(in_A[23:16]), .b(in_B[23:16]), .out(out_F[23:16]), .cin(adder_2_cout), .cout(adder_3_cout));
  Adder adder_4 (.a(in_A[31:24]), .b(in_B[31:24]), .out(out_F[31:24]), .cin(adder_3_cout), .cout(adder_4_cout));
  xor a (out_OF, adder_4_cout, adder_3_cout);
  mux8_msb msb (.in_1(out_F[31:24]), .out_2(out_SF));
  nor32 c (.in_1(out_F[7:0]), .in_2(out_F[15:8]), .in_3(out_F[23:16]), .in_4(out_F[31:24]), .out_5(out_ZF));
  xor b (out_CF, in_Cin, adder_4_cout);

  // Notes on the sheet:
  //   fork3,8 deleted
  //   0
  //   0
  //   1
  //   2
  //   1
  //   7
  //   3
  //   2
  //   4
  //   5
  //   6
endmodule

module nor32 (
  input  [7:0] in_1,
  input  [7:0] in_2,
  input  [7:0] in_3,
  input  [7:0] in_4,
  output out_5
);

  wire or_2_out;
  wire [7:0] or_1_out;

  assign or_1_out = in_1 | in_2 | in_3 | in_4;  // OR_Gate or_1, 8 bits wide
  or or_2 (or_2_out, or_1_out[0], or_1_out[1], or_1_out[2], or_1_out[3], or_1_out[4], or_1_out[5], or_1_out[6], or_1_out[7]);
  not not_1 (out_5, or_2_out);
endmodule

module mux8_msb (
  input  [7:0] in_1,
  output out_2
);

  BitSelector bitselector_1 (.in(in_1), .out(out_2), .sel(3'b111));
endmodule

module ALU (
  input  [4:0] in_shamt,
  input  [31:0] in_A,
  input  [31:0] in_B,
  input  [2:0] ALUctr,
  output out_Zero,
  output out_Overflow,
  output [31:0] out_Result
);

  wire adder32_1_out_cf, adder32_1_out_of, adder32_1_out_sf, multiplexer_3_out, xor_2_out, xor_3_out;
  wire [4:0] pla_1_out;
  wire [31:0] adder32_1_out_f, bit_extender_1_out, multiplexer_1_out, or_1_out, shifter_1_out, xor_1_out;

  PLA #(.in_width(3), .out_width(5), .\table ("000 00000 # addu\n001 01000 # add\n010 00001 # or\n100 10000 # subu\n101 11000 # sub\n110 10010 # sltu\n111 10110 # slt\n011 00011 # sll")) pla_1 (
    .in(ALUctr), .out(pla_1_out));
  assign bit_extender_1_out = {{31{pla_1_out[4]}}, pla_1_out[4]};  // Bit_Extender bit_extender_1
  assign xor_1_out = in_B ^ bit_extender_1_out;  // XOR_Gate xor_1, 32 bits wide
  assign or_1_out = in_A | in_B;  // OR_Gate or_1, 32 bits wide
  adder32 adder32_1 (
    .in_Cin(pla_1_out[4]), .in_A(in_A), .in_B(xor_1_out), .out_F(adder32_1_out_f), .out_SF(adder32_1_out_sf),
    .out_CF(adder32_1_out_cf), .out_ZF(out_Zero), .out_OF(adder32_1_out_of));
  Multiplexer #(.width(32)) multiplexer_1 (
    .in0({32{1'b0}}), .in1(32'h1), .out(multiplexer_1_out), .sel(multiplexer_3_out));
  Shifter #(.width(32)) shifter_1 (.in(in_B), .\dist (in_shamt), .out(shifter_1_out));
  xor xor_2 (xor_2_out, pla_1_out[4], adder32_1_out_cf);
  xor xor_3 (xor_3_out, adder32_1_out_sf, adder32_1_out_of);
  Multiplexer #(.select(2), .width(32)) multiplexer_2 (
    .in0(adder32_1_out_f), .in1(or_1_out), .in2(multiplexer_1_out), .in3(shifter_1_out), .out(out_Result),
    .sel(pla_1_out[1:0]));
  Multiplexer multiplexer_3 (.in0(xor_2_out), .in1(xor_3_out), .out(multiplexer_3_out), .sel(pla_1_out[2]));
  and and_1 (out_Overflow, adder32_1_out_of, pla_1_out[3]);

  // Notes on the sheet:
  //   0-1:OP, 2:SIG, 3:OV, 4:SUB
endmodule

module instr_fetch (
  input  clk,
  input  [15:0] in_imm16,
  input  clr,
  input  in_Branch,
  input  in_Zero,
  output [31:0] instr,
  output [5:0] instr_func,
  output [4:0] instr_shamt,
  output [4:0] instr_Rd,
  output [4:0] instr_Rt,
  output [4:0] instr_Rs,
  output [5:0] instr_Op,
  output [15:0] instr_Imm16,
  output [25:0] instr_target
);

  wire [0:0] and_1_out;
  wire [7:0] bit_extender_2_out;
  wire [29:0] adder_1_out, adder_2_out, bit_extender_1_out, multiplexer_1_out, PC_q;

  Register #(.width(30)) PC (.D(multiplexer_1_out), .clk(clk), .Q(PC_q));  // open: en, clr
  Adder #(.width(30)) adder_1 (.a(PC_q), .b(30'h1), .out(adder_1_out));  // open: cin, cout
  assign bit_extender_1_out = {{14{in_imm16[15]}}, in_imm16};  // Bit_Extender bit_extender_1
  Adder #(.width(30)) adder_2 (.a(adder_1_out), .b(bit_extender_1_out), .out(adder_2_out));  // open: cin, cout
  Multiplexer #(.select(2), .width(30)) multiplexer_1 (
    .in0(adder_1_out), .in1(adder_2_out), .in2({30{1'b0}}), .in3({30{1'b0}}), .out(multiplexer_1_out),
    .sel({clr, and_1_out[0]}));
  and and_1 (and_1_out[0], in_Branch, in_Zero);
  Bit_Extender #(.in_width(30), .out_width(8)) bit_extender_2 (.in(PC_q), .out(bit_extender_2_out));
  RAM #(.dataWidth(32)) ram_1 (.addr(bit_extender_2_out), .clk(clk), .dout(instr));  // open: we, oe, din

  assign instr_func = instr[5:0];
  assign instr_Imm16 = instr[15:0];
  assign instr_Op = instr[31:26];
  assign instr_Rd = instr[15:11];
  assign instr_Rs = instr[25:21];
  assign instr_Rt = instr[20:16];
  assign instr_shamt = instr[10:6];
  assign instr_target = instr[25:0];
endmodule

module main (
  input  in_1,
  input  in_2,
  output [31:0] out_3
);

  wire ALUsrc, and_1_out, and_2_out, Branch, clk, ExtOp, Jump, MemtoReg, MemWr, not_1_out, Overflow, RegDst,
       RegWr, Rtype, Zero;
  wire [2:0] ALUctl;
  wire [4:0] multiplexer_2_out;
  wire [7:0] bit_extender_4_out, bit_extender_5_out;
  wire [29:0] adder_1_out, adder_2_out, bit_extender_1_out, multiplexer_3_out, multiplexer_4_out, PC_q;
  wire [31:0] ALUresult, bit_extender_2_out, bit_extender_3_out, BusA, BusB, BusW, multiplexer_1_out,
       multiplexer_5_out, multiplexer_6_out, ram_2_dout;

  Clock clock_1 (.out(clk));
  Register #(.width(30)) PC (.D(multiplexer_4_out), .clk(clk), .Q(PC_q), .clr(in_1));  // open: en
  Multiplexer #(.width(32)) multiplexer_1 (.in0(BusW), .in1({32{1'b0}}), .out(multiplexer_1_out), .sel(in_1));
  not not_1 (not_1_out, Overflow);
  and and_1 (and_1_out, RegWr, not_1_out);
  mips_decoder mips_decoder_1 (
    .in_op(out_3[31:26]), .in_func(out_3[5:0]), .Rtype(Rtype), .RegWr(RegWr), .ALUsrc(ALUsrc),
    .RegDst(RegDst), .MemtoReg(MemtoReg), .MemWr(MemWr), .Branch(Branch), .Jump(Jump), .ExtOp(ExtOp),
    .ALUctl(ALUctl));
  Multiplexer #(.width(5)) multiplexer_2 (
    .in0(out_3[20:16]), .in1(out_3[15:11]), .out(multiplexer_2_out), .sel(RegDst));
  Adder #(.width(30)) adder_1 (.a(PC_q), .b(30'h1), .out(adder_1_out));  // open: cin, cout
  assign bit_extender_1_out = {{14{out_3[15]}}, out_3[15:0]};  // Bit_Extender bit_extender_1
  Adder #(.width(30)) adder_2 (.a(adder_1_out), .b(bit_extender_1_out), .out(adder_2_out));  // open: cin, cout
  reg32 reg32_1 (
    .clear(in_1), .in_Ra(out_3[25:21]), .in_Rb(out_3[20:16]), .in_Rw(multiplexer_2_out), .in_WE(and_1_out),
    .in_Rwdata(multiplexer_1_out), .clk(clk), .out_Ra(BusA), .out_Rb(BusB));
  and and_2 (and_2_out, Branch, Zero);
  Multiplexer #(.width(30)) multiplexer_3 (
    .in0(adder_1_out), .in1(adder_2_out), .out(multiplexer_3_out), .sel(and_2_out));
  Multiplexer #(.width(30)) multiplexer_4 (
    .in0(multiplexer_3_out), .in1({30{1'b0}}), .out(multiplexer_4_out), .sel(in_2));
  assign bit_extender_2_out = {{16{1'b0}}, out_3[15:0]};  // Bit_Extender bit_extender_2
  assign bit_extender_3_out = {{16{out_3[15]}}, out_3[15:0]};  // Bit_Extender bit_extender_3
  Bit_Extender #(.in_width(30), .out_width(8)) bit_extender_4 (.in(PC_q), .out(bit_extender_4_out));
  Multiplexer #(.width(32)) multiplexer_5 (
    .in0(bit_extender_2_out), .in1(bit_extender_3_out), .out(multiplexer_5_out), .sel(ExtOp));
  RAM #(.dataWidth(32), .trigger("falling")) ram_1 (
    .addr(bit_extender_4_out), .clk(clk), .dout(out_3));  // open: we, oe, din
  Multiplexer #(.width(32)) multiplexer_6 (.in0(BusB), .in1(multiplexer_5_out), .out(multiplexer_6_out), .sel(ALUsrc));
  ALU alu_1 (
    .in_shamt(out_3[10:6]), .in_A(BusA), .in_B(multiplexer_6_out), .ALUctr(ALUctl), .out_Zero(Zero),
    .out_Overflow(Overflow), .out_Result(ALUresult));
  Bit_Extender #(.in_width(32), .out_width(8), .\type ("zero")) bit_extender_5 (
    .in(ALUresult), .out(bit_extender_5_out));
  RAM #(.dataWidth(32), .trigger("falling")) ram_2 (
    .addr(bit_extender_5_out), .we(MemWr), .clk(clk), .din(BusB), .dout(ram_2_dout));  // open: oe
  Multiplexer #(.width(32)) multiplexer_7 (.in0(ALUresult), .in1(ram_2_dout), .out(BusW), .sel(MemtoReg));

  // Other names for the same wires on the sheet: clr = in_1; func[5:0] = out_3[5:0]; Imm16[15:0] = out_3[15:0];
  //   instr[31:0] = out_3; Target[25:0] = out_3[25:0]; shamt[4:0] = out_3[10:6]; Rd[4:0] = out_3[15:11];
  //   Rt[4:0] = out_3[20:16]; Rs[4:0] = out_3[25:21]; Op[5:0] = out_3[31:26]
endmodule

module reg32 (
  input  clear,
  input  [4:0] in_Ra,
  input  [4:0] in_Rb,
  input  [4:0] in_Rw,
  input  in_WE,
  input  [31:0] in_Rwdata,
  input  clk,
  output [31:0] out_Ra,
  output [31:0] out_Rb
);

  wire decoder_1_out0, decoder_1_out1, decoder_1_out2, decoder_1_out3;
  wire [31:0] reg8_0locked_1_out_r1data, reg8_0locked_1_out_r2data, reg8_1_out_r1data, reg8_1_out_r2data,
       reg8_2_out_r1data, reg8_2_out_r2data, reg8_3_out_r1data, reg8_3_out_r2data;

  Decoder #(.select(2)) decoder_1 (
    .out0(decoder_1_out0), .out1(decoder_1_out1), .out2(decoder_1_out2), .out3(decoder_1_out3),
    .sel(in_Rw[4:3]), .en(in_WE));
  reg8_0locked reg8_0locked_1 (
    .in_Rwdata(in_Rwdata), .clk(clk), .in_WE(decoder_1_out0), .in_Rwaddr(in_Rw[2:0]), .clear(clear),
    .in_R1addr(in_Rb[2:0]), .in_R2addr(in_Ra[2:0]), .out_R1data(reg8_0locked_1_out_r1data),
    .out_R2data(reg8_0locked_1_out_r2data));
  reg8 reg8_1 (
    .in_Rwdata(in_Rwdata), .clk(clk), .in_WE(decoder_1_out1), .in_Rwaddr(in_Rw[2:0]), .clear(clear),
    .in_R1addr(in_Rb[2:0]), .in_R2addr(in_Ra[2:0]), .out_R1data(reg8_1_out_r1data),
    .out_R2data(reg8_1_out_r2data));
  reg8 reg8_2 (
    .in_Rwdata(in_Rwdata), .clk(clk), .in_WE(decoder_1_out2), .in_Rwaddr(in_Rw[2:0]), .clear(clear),
    .in_R1addr(in_Rb[2:0]), .in_R2addr(in_Ra[2:0]), .out_R1data(reg8_2_out_r1data),
    .out_R2data(reg8_2_out_r2data));
  reg8 reg8_3 (
    .in_Rwdata(in_Rwdata), .clk(clk), .in_WE(decoder_1_out3), .in_Rwaddr(in_Rw[2:0]), .clear(clear),
    .in_R1addr(in_Rb[2:0]), .in_R2addr(in_Ra[2:0]), .out_R1data(reg8_3_out_r1data),
    .out_R2data(reg8_3_out_r2data));
  Multiplexer #(.select(2), .width(32)) multiplexer_1 (
    .in0(reg8_0locked_1_out_r1data), .in1(reg8_1_out_r1data), .in2(reg8_2_out_r1data),
    .in3(reg8_3_out_r1data), .out(out_Ra), .sel(in_Ra[4:3]));
  Multiplexer #(.select(2), .width(32)) multiplexer_2 (
    .in0(reg8_0locked_1_out_r2data), .in1(reg8_1_out_r2data), .in2(reg8_2_out_r2data),
    .in3(reg8_3_out_r2data), .out(out_Rb), .sel(in_Rb[4:3]));
endmodule

module reg8 (
  input  [31:0] in_Rwdata,
  input  clk,
  input  in_WE,
  input  [2:0] in_Rwaddr,
  input  clear,
  input  [2:0] in_R1addr,
  input  [2:0] in_R2addr,
  output [31:0] out_R1data,
  output [31:0] out_R2data
);

  wire decoder_1_out0, decoder_1_out1, decoder_1_out2, decoder_1_out3, decoder_1_out4, decoder_1_out5,
       decoder_1_out6, decoder_1_out7;
  wire [31:0] reg0_q, reg1_q, reg2_q, reg3_q, reg4_q, reg5_q, reg6_q, reg7_q;

  Decoder #(.select(3)) decoder_1 (
    .out0(decoder_1_out0), .out1(decoder_1_out1), .out2(decoder_1_out2), .out3(decoder_1_out3),
    .out4(decoder_1_out4), .out5(decoder_1_out5), .out6(decoder_1_out6), .out7(decoder_1_out7),
    .sel(in_Rwaddr), .en(in_WE));
  Register #(.trigger("falling"), .width(32)) reg0 (
    .D(in_Rwdata), .en(decoder_1_out0), .clk(clk), .Q(reg0_q), .clr(clear));
  Register #(.trigger("falling"), .width(32)) reg1 (
    .D(in_Rwdata), .en(decoder_1_out1), .clk(clk), .Q(reg1_q), .clr(clear));
  Register #(.trigger("falling"), .width(32)) reg2 (
    .D(in_Rwdata), .en(decoder_1_out2), .clk(clk), .Q(reg2_q), .clr(clear));
  Register #(.trigger("falling"), .width(32)) reg3 (
    .D(in_Rwdata), .en(decoder_1_out3), .clk(clk), .Q(reg3_q), .clr(clear));
  Register #(.trigger("falling"), .width(32)) reg4 (
    .D(in_Rwdata), .en(decoder_1_out4), .clk(clk), .Q(reg4_q), .clr(clear));
  Register #(.trigger("falling"), .width(32)) reg5 (
    .D(in_Rwdata), .en(decoder_1_out5), .clk(clk), .Q(reg5_q), .clr(clear));
  Register #(.trigger("falling"), .width(32)) reg6 (
    .D(in_Rwdata), .en(decoder_1_out6), .clk(clk), .Q(reg6_q), .clr(clear));
  Register #(.trigger("falling"), .width(32)) reg7 (
    .D(in_Rwdata), .en(decoder_1_out7), .clk(clk), .Q(reg7_q), .clr(clear));
  Multiplexer #(.select(3), .width(32)) multiplexer_1 (
    .in0(reg0_q), .in1(reg1_q), .in2(reg2_q), .in3(reg3_q), .in4(reg4_q), .in5(reg5_q), .in6(reg6_q),
    .in7(reg7_q), .out(out_R1data), .sel(in_R1addr));
  Multiplexer #(.select(3), .width(32)) multiplexer_2 (
    .in0(reg0_q), .in1(reg1_q), .in2(reg2_q), .in3(reg3_q), .in4(reg4_q), .in5(reg5_q), .in6(reg6_q),
    .in7(reg7_q), .out(out_R2data), .sel(in_R2addr));
endmodule

module mips_decoder (
  input  [5:0] in_op,
  input  [5:0] in_func,
  output Rtype,
  output RegWr,
  output ALUsrc,
  output RegDst,
  output MemtoReg,
  output MemWr,
  output Branch,
  output Jump,
  output ExtOp,
  output [2:0] ALUctl
);

  wire addiu_out, not_1_out, not_2_out, not_3_out, not_4_out, not_5_out, not_6_out, not_7_out, not_8_out,
       not_9_out, not_10_out, not_11_out, not_12_out, not_13_out, not_14_out, not_15_out, not_16_out,
       not_17_out, not_18_out, not_19_out, not_20_out, not_21_out, not_22_out, not_23_out, not_24_out,
       not_25_out, not_26_out, not_27_out, not_28_out;
  wire [1:1] ori_out;
  wire [2:0] ALU_ctrler_out;

  PLA #(.in_width(6), .out_width(3), .\table ("100000 001\n100010 101\n100011 100\n101010 111\n101011 110\n000000 011 # sll")) ALU_ctrler (
    .in(in_func), .out(ALU_ctrler_out));
  Multiplexer #(.width(3)) multiplexer_1 (
    .in0({Branch, ori_out[1], 1'b0}), .in1(ALU_ctrler_out), .out(ALUctl), .sel(RegDst));
  not not_1 (not_1_out, in_op[5]);
  not not_2 (not_2_out, in_op[4]);
  not not_3 (not_3_out, in_op[3]);
  not not_4 (not_4_out, in_op[2]);
  not not_5 (not_5_out, in_op[1]);
  not not_6 (not_6_out, in_op[0]);
  and R_ty (RegDst, not_1_out, not_2_out, not_3_out, not_4_out, not_5_out, not_6_out);
  not not_7 (not_7_out, in_op[5]);
  not not_8 (not_8_out, in_op[4]);
  and ori (ori_out[1], not_7_out, not_8_out, in_op[3], in_op[2], not_9_out, in_op[0]);
  not not_9 (not_9_out, in_op[1]);
  not not_10 (not_10_out, in_op[5]);
  not not_11 (not_11_out, in_op[4]);
  not not_12 (not_12_out, in_op[2]);
  not not_13 (not_13_out, in_op[1]);
  and addiu (addiu_out, not_10_out, not_11_out, in_op[3], not_12_out, not_13_out, in_op[0]);
  not not_14 (not_14_out, in_op[2]);
  not not_15 (not_15_out, in_op[4]);
  not not_16 (not_16_out, in_op[3]);
  and lw (MemtoReg, in_op[5], not_15_out, not_16_out, not_14_out, in_op[1], in_op[0]);
  not not_17 (not_17_out, in_op[4]);
  and sw (MemWr, in_op[5], not_17_out, in_op[3], not_18_out, in_op[1], in_op[0]);
  not not_18 (not_18_out, in_op[2]);
  not not_19 (not_19_out, in_op[5]);
  not not_20 (not_20_out, in_op[4]);
  not not_21 (not_21_out, in_op[3]);
  not not_22 (not_22_out, in_op[1]);
  not not_23 (not_23_out, in_op[0]);
  and beq (Branch, not_19_out, not_20_out, not_21_out, in_op[2], not_22_out, not_23_out);
  not not_24 (not_24_out, in_op[5]);
  not not_25 (not_25_out, in_op[4]);
  not not_26 (not_26_out, in_op[3]);
  not not_27 (not_27_out, in_op[2]);
  and is_jump (Jump, not_24_out, not_25_out, not_26_out, not_27_out, in_op[1], not_28_out);
  not not_28 (not_28_out, in_op[0]);
  or or_1 (RegWr, RegDst, ori_out[1], addiu_out, MemtoReg);
  or or_2 (ALUsrc, ori_out[1], addiu_out, MemtoReg, MemWr);
  or or_3 (ExtOp, addiu_out, MemtoReg, MemWr);

  assign Rtype = RegDst;

  // Notes on the sheet:
  //   ALUop
  //   1:sign, 0:zero
endmodule

module reg8_0locked (
  input  [31:0] in_Rwdata,
  input  clk,
  input  in_WE,
  input  [2:0] in_Rwaddr,
  input  clear,
  input  [2:0] in_R1addr,
  input  [2:0] in_R2addr,
  output [31:0] out_R1data,
  output [31:0] out_R2data
);

  wire decoder_1_out1, decoder_1_out2, decoder_1_out3, decoder_1_out4, decoder_1_out5, decoder_1_out6,
       decoder_1_out7;
  wire [31:0] reg0_q, reg1_q, reg2_q, reg3_q, reg4_q, reg5_q, reg6_q, reg7_q;

  Decoder #(.select(3)) decoder_1 (
    .out1(decoder_1_out1), .out2(decoder_1_out2), .out3(decoder_1_out3), .out4(decoder_1_out4),
    .out5(decoder_1_out5), .out6(decoder_1_out6), .out7(decoder_1_out7), .sel(in_Rwaddr), .en(in_WE));  // open: out0
  Register #(.width(32)) reg0 (.clk(clk), .Q(reg0_q), .clr(1'b1));  // open: D, en
  Register #(.width(32)) reg1 (.D(in_Rwdata), .en(decoder_1_out1), .clk(clk), .Q(reg1_q), .clr(clear));
  Register #(.width(32)) reg2 (.D(in_Rwdata), .en(decoder_1_out2), .clk(clk), .Q(reg2_q), .clr(clear));
  Register #(.width(32)) reg3 (.D(in_Rwdata), .en(decoder_1_out3), .clk(clk), .Q(reg3_q), .clr(clear));
  Register #(.width(32)) reg4 (.D(in_Rwdata), .en(decoder_1_out4), .clk(clk), .Q(reg4_q), .clr(clear));
  Register #(.width(32)) reg5 (.D(in_Rwdata), .en(decoder_1_out5), .clk(clk), .Q(reg5_q), .clr(clear));
  Register #(.width(32)) reg6 (.D(in_Rwdata), .en(decoder_1_out6), .clk(clk), .Q(reg6_q), .clr(clear));
  Register #(.width(32)) reg7 (.D(in_Rwdata), .en(decoder_1_out7), .clk(clk), .Q(reg7_q), .clr(clear));
  Multiplexer #(.select(3), .width(32)) multiplexer_1 (
    .in0(reg0_q), .in1(reg1_q), .in2(reg2_q), .in3(reg3_q), .in4(reg4_q), .in5(reg5_q), .in6(reg6_q),
    .in7(reg7_q), .out(out_R1data), .sel(in_R1addr));
  Multiplexer #(.select(3), .width(32)) multiplexer_2 (
    .in0(reg0_q), .in1(reg1_q), .in2(reg2_q), .in3(reg3_q), .in4(reg4_q), .in5(reg5_q), .in6(reg6_q),
    .in7(reg7_q), .out(out_R2data), .sel(in_R2addr));
endmodule
